// Logisim project ALU_javor.circ as structural Verilog: 14 circuits, main circuit main
module main (
  input  [3:0] in_1,
  input  in_2,
  output [7:0] out_3
);

  wire alu_8_bit_1_cout, alu_8_bit_1_zero;
  wire [7:0] register_1_q, register_2_q;

  Register register_1 (.Q(register_1_q));  // open: D, en, clk, clr
  Register register_2 (.Q(register_2_q));  // open: D, en, clk, clr
  ALU___8_bit alu_8_bit_1 (
    .A(register_1_q), .B(register_2_q), .CIN(in_2), .OUT(out_3), .ZERO(alu_8_bit_1_zero),
    .COUT(alu_8_bit_1_cout), .SEL(in_1));
  Hex_Digit_Display hex_digit_display_1 (.value(out_3[7:4]));  // open: dp
  LED led_1 (.in(alu_8_bit_1_zero));
  LED led_2 (.in(alu_8_bit_1_cout));
  Hex_Digit_Display hex_digit_display_2 (.value(out_3[3:0]));  // open: dp
endmodule

module adder1 (
  input  A,
  input  B,
  output X,
  output Cout
);

  xor xor_1 (X, A, B);
  and and_1 (Cout, A, B);
endmodule

module full_adder (
  input  Cin,
  input  A,
  input  B,
  output X,
  output Cout
);

  wire adder1_1_cout, adder1_1_x, adder1_2_cout;

  adder1 adder1_1 (.A(A), .B(B), .X(adder1_1_x), .Cout(adder1_1_cout));
  Pull_Resistor pull_resistor_1 (.node(Cin));
  adder1 adder1_2 (.A(adder1_1_x), .B(Cin), .X(X), .Cout(adder1_2_cout));
  or or_1 (Cout, adder1_2_cout, adder1_1_cout);
endmodule

module adder8 (
  input  [7:0] in_1,
  input  [7:0] in_2,
  input  Cin,
  output [7:0] out_4,
  output Cout
);

  wire full_adder_1_cout, full_adder_2_cout, full_adder_3_cout, full_adder_4_cout, full_adder_5_cout,
       full_adder_6_cout, full_adder_7_cout;

  Pull_Resistor pull_resistor_1 (.node(in_2));
  Pull_Resistor pull_resistor_2 (.node(Cin));
  full_adder full_adder_1 (.A(in_1[0]), .B(in_2[0]), .X(out_4[0]), .Cin(Cin), .Cout(full_adder_1_cout));
  full_adder full_adder_2 (.A(in_1[1]), .B(in_2[1]), .X(out_4[1]), .Cin(full_adder_1_cout), .Cout(full_adder_2_cout));
  full_adder full_adder_3 (.A(in_1[2]), .B(in_2[2]), .X(out_4[2]), .Cin(full_adder_2_cout), .Cout(full_adder_3_cout));
  full_adder full_adder_4 (.A(in_1[3]), .B(in_2[3]), .X(out_4[3]), .Cin(full_adder_3_cout), .Cout(full_adder_4_cout));
  full_adder full_adder_5 (.A(in_1[4]), .B(in_2[4]), .X(out_4[4]), .Cin(full_adder_4_cout), .Cout(full_adder_5_cout));
  full_adder full_adder_6 (.A(in_1[5]), .B(in_2[5]), .X(out_4[5]), .Cin(full_adder_5_cout), .Cout(full_adder_6_cout));
  full_adder full_adder_7 (.A(in_1[6]), .B(in_2[6]), .X(out_4[6]), .Cin(full_adder_6_cout), .Cout(full_adder_7_cout));
  full_adder full_adder_8 (.A(in_1[7]), .B(in_2[7]), .X(out_4[7]), .Cin(full_adder_7_cout), .Cout(Cout));

  // Notes on the sheet:
  //   X
endmodule

module ALU___8_bit (
  input  [7:0] A,
  input  [7:0] B,
  input  CIN,
  input  [3:0] SEL,
  output [7:0] OUT,
  output ZERO,
  output COUT
);

  wire ADD, addsub8_1_cout, AND, DEC, INC, NOT, OR, or_1_out, or_2_out, or_4_out, ROTL, rotl_1_cout, ROTR,
       rotr_1_cout, SHL, shl_1_cout, SHR, shr_1_cout, SUB, XOR;
  wire [7:0] addsub8_1_out_5, and_1_out, multiplexer_1_out, not_1_out, or_3_out, rotl_1_out_2, rotr_1_out_3,
       shl_1_out_3, shr_1_out_4, xor_1_out;

  instruction instruction_1 (
    .in_1(SEL), .XOR(XOR), .OR(OR), .AND(AND), .NOT(NOT), .SHL(SHL), .SHR(SHR), .ROTL(ROTL), .ROTR(ROTR),
    .ADD(ADD), .SUB(SUB), .INC(INC), .DEC(DEC));  // open: MUL
  Multiplexer #(.width(8), .enable("false")) multiplexer_1 (
    .in0(B), .in1(8'h1), .out(multiplexer_1_out), .sel(or_2_out));
  or or_1 (or_1_out, SUB, DEC);
  or or_2 (or_2_out, DEC, INC);
  assign xor_1_out = A ^ B;  // XOR_Gate xor_1, 8 bits wide
  assign or_3_out = A | B;  // OR_Gate or_3, 8 bits wide
  assign and_1_out = A & B;  // AND_Gate and_1, 8 bits wide
  assign not_1_out = ~A;  // NOT_Gate not_1, 8 bits wide
  SHL shl_1 (.A(A), .out_3(shl_1_out_3), .COUT(shl_1_cout), .CIN(CIN));
  SHR shr_1 (.A(A), .COUT(shr_1_cout), .out_4(shr_1_out_4), .CIN(CIN));
  rotl rotl_1 (.A(A), .out_2(rotl_1_out_2), .COUT(rotl_1_cout));
  rotr rotr_1 (.A(A), .COUT(rotr_1_cout), .out_3(rotr_1_out_3));
  addSub8 addsub8_1 (
    .in_3(A), .in_4(multiplexer_1_out), .SUB(or_1_out), .out_5(addsub8_1_out_5), .COUT(addsub8_1_cout),
    .CIN(CIN));
  assign COUT = SHL ? shl_1_cout : 1'bz;  // Controlled_Buffer controlled_buffer_1
  assign COUT = SHR ? shr_1_cout : 1'bz;  // Controlled_Buffer controlled_buffer_2
  assign COUT = ROTL ? rotl_1_cout : 1'bz;  // Controlled_Buffer controlled_buffer_3
  assign COUT = ROTR ? rotr_1_cout : 1'bz;  // Controlled_Buffer controlled_buffer_4
  or or_4 (or_4_out, ADD, or_1_out, or_2_out);
  assign OUT = or_4_out ? addsub8_1_out_5 : 8'bz;  // Controlled_Buffer controlled_buffer_5
  assign COUT = or_4_out ? addsub8_1_cout : 1'bz;  // Controlled_Buffer controlled_buffer_6
  assign OUT = XOR ? xor_1_out : 8'bz;  // Controlled_Buffer controlled_buffer_7
  assign OUT = OR ? or_3_out : 8'bz;  // Controlled_Buffer controlled_buffer_8
  assign OUT = AND ? and_1_out : 8'bz;  // Controlled_Buffer controlled_buffer_9
  assign OUT = NOT ? not_1_out : 8'bz;  // Controlled_Buffer controlled_buffer_10
  assign OUT = SHL ? shl_1_out_3 : 8'bz;  // Controlled_Buffer controlled_buffer_11
  assign OUT = SHR ? shr_1_out_4 : 8'bz;  // Controlled_Buffer controlled_buffer_12
  assign OUT = ROTL ? rotl_1_out_2 : 8'bz;  // Controlled_Buffer controlled_buffer_13
  assign OUT = ROTR ? rotr_1_out_3 : 8'bz;  // Controlled_Buffer controlled_buffer_14
  nor nor_1 (ZERO, OUT[0], OUT[1], OUT[2], OUT[3], OUT[4], OUT[5], OUT[6], OUT[7]);
endmodule

module SHR (
  input  [7:0] A,
  input  CIN,
  output COUT,
  output [7:0] out_4
);

  Pull_Resistor pull_resistor_1 (.node(CIN));

  assign COUT = A[0];
  assign out_4 = {CIN, A[7:1]};

  // Notes on the sheet:
  //   OUT
endmodule

module SHL (
  input  CIN,
  input  [7:0] A,
  output [7:0] out_3,
  output COUT
);

  Pull_Resistor pull_resistor_1 (.node(CIN));

  assign COUT = A[7];
  assign out_3 = {A[6:0], CIN};

  // Notes on the sheet:
  //   OUT
endmodule

module instruction (
  input  [3:0] in_1,
  output XOR,
  output OR,
  output AND,
  output NOT,
  output SHL,
  output SHR,
  output ROTL,
  output ROTR,
  output ADD,
  output SUB,
  output INC,
  output DEC,
  output MUL
);

  and and_1 (XOR, ~in_1[0], ~in_1[1], ~in_1[2], ~in_1[3]);  // AND_Gate
  and and_2 (OR, in_1[0], ~in_1[1], ~in_1[2], ~in_1[3]);  // AND_Gate
  and and_3 (AND, ~in_1[0], in_1[1], ~in_1[2], ~in_1[3]);  // AND_Gate
  and and_4 (NOT, in_1[0], in_1[1], ~in_1[2], ~in_1[3]);  // AND_Gate
  and and_5 (SHL, ~in_1[0], ~in_1[1], in_1[2], ~in_1[3]);  // AND_Gate
  and and_6 (SHR, in_1[0], ~in_1[1], in_1[2], ~in_1[3]);  // AND_Gate
  and and_7 (ROTL, ~in_1[0], in_1[1], in_1[2], ~in_1[3]);  // AND_Gate
  and and_8 (ROTR, in_1[0], in_1[1], in_1[2], ~in_1[3]);  // AND_Gate
  and and_9 (ADD, ~in_1[0], ~in_1[1], ~in_1[2], in_1[3]);  // AND_Gate
  and and_10 (SUB, in_1[0], ~in_1[1], ~in_1[2], in_1[3]);  // AND_Gate
  and and_11 (INC, ~in_1[0], in_1[1], ~in_1[2], in_1[3]);  // AND_Gate
  and and_12 (DEC, in_1[0], in_1[1], ~in_1[2], in_1[3]);  // AND_Gate
  and and_13 (MUL, ~in_1[0], ~in_1[1], in_1[2], in_1[3]);  // AND_Gate
endmodule

module addSub8 (
  input  SUB,
  input  CIN,
  input  [7:0] in_3,
  input  [7:0] in_4,
  output [7:0] out_5,
  output COUT
);

  wire or_1_out;
  wire [7:0] xor_1_out;

  assign xor_1_out = {8{SUB}} ^ in_4;  // XOR_Gate xor_1, 8 bits wide
  or or_1 (or_1_out, CIN, SUB);
  adder8 adder8_1 (.in_1(in_3), .in_2(xor_1_out), .out_4(out_5), .Cin(or_1_out), .Cout(COUT));

  // Notes on the sheet:
  //   A
  //   B
  //   X
endmodule

module mul8 (
  input  [7:0] in_1,
  input  [7:0] in_2,
  output [7:0] out_3
);

  wire and_2_out, and_3_out, and_4_out, and_5_out, and_6_out, and_7_out, and_11_out, and_12_out, and_13_out,
       and_14_out, and_15_out, and_18_out, and_19_out, and_20_out, and_21_out, and_22_out, and_23_out,
       and_24_out, and_25_out, and_26_out, and_27_out, and_28_out, and_29_out, and_30_out, and_31_out,
       and_32_out, and_33_out, and_34_out, and_35_out, and_36_out, full_adder_1_cout, full_adder_2_cout,
       full_adder_2_x;

  and and_1 (out_3[0], in_2[0], in_1[0]);
  and and_2 (and_2_out, in_2[0], in_1[1]);
  and and_3 (and_3_out, in_2[1], in_1[0]);
  and and_4 (and_4_out, in_2[0], in_1[2]);
  and and_5 (and_5_out, in_2[1], in_1[1]);
  and and_6 (and_6_out, in_2[2], in_1[0]);
  and and_7 (and_7_out, in_2[0], in_1[3]);
  // AND_Gate and_8 has open pins: in0=in_2[1], in1=in_1[2], out=open
  // AND_Gate and_9 has open pins: in0=in_2[2], in1=in_1[1], out=open
  // AND_Gate and_10 has open pins: in0=in_2[3], in1=in_1[0], out=open
  and and_11 (and_11_out, in_2[0], in_1[4]);
  and and_12 (and_12_out, in_2[1], in_1[3]);
  and and_13 (and_13_out, in_2[2], in_1[2]);
  and and_14 (and_14_out, in_2[3], in_1[1]);
  and and_15 (and_15_out, in_2[4], in_1[0]);
  // AND_Gate and_16 has open pins: in0=in_2[0], in1=in_1[5], out=open
  // AND_Gate and_17 has open pins: in0=in_2[1], in1=in_1[4], out=open
  and and_18 (and_18_out, in_2[2], in_1[3]);
  and and_19 (and_19_out, in_2[3], in_1[2]);
  and and_20 (and_20_out, in_2[4], in_1[1]);
  and and_21 (and_21_out, in_2[5], in_1[0]);
  and and_22 (and_22_out, in_2[0], in_1[6]);
  and and_23 (and_23_out, in_2[1], in_1[5]);
  and and_24 (and_24_out, in_2[2], in_1[4]);
  and and_25 (and_25_out, in_2[3], in_1[3]);
  and and_26 (and_26_out, in_2[4], in_1[2]);
  and and_27 (and_27_out, in_2[5], in_1[1]);
  and and_28 (and_28_out, in_2[6], in_1[0]);
  and and_29 (and_29_out, in_2[0], in_1[7]);
  and and_30 (and_30_out, in_2[1], in_1[6]);
  and and_31 (and_31_out, in_2[2], in_1[5]);
  and and_32 (and_32_out, in_2[3], in_1[4]);
  and and_33 (and_33_out, in_2[4], in_1[3]);
  and and_34 (and_34_out, in_2[5], in_1[2]);
  and and_35 (and_35_out, in_2[6], in_1[1]);
  and and_36 (and_36_out, in_2[7], in_1[0]);
  // AND_Gate and_37 is placed but not wired
  // AND_Gate and_38 is placed but not wired
  // AND_Gate and_39 is placed but not wired
  // AND_Gate and_40 is placed but not wired
  // AND_Gate and_41 is placed but not wired
  // AND_Gate and_42 is placed but not wired
  full_adder full_adder_1 (.A(and_2_out), .B(and_3_out), .X(out_3[1]), .Cout(full_adder_1_cout));  // open: Cin
  full_adder full_adder_2 (
    .A(and_4_out), .B(and_5_out), .X(full_adder_2_x), .Cin(full_adder_1_cout), .Cout(full_adder_2_cout));
  full_adder full_adder_3 (.A(full_adder_2_x), .B(and_6_out), .X(out_3[2]), .Cin(full_adder_2_cout));  // open: Cout
  // OR_Gate or_1 has open pins: out=out_3[6]
endmodule

module mux (
  input  in_1,
  input  in_2,
  input  in_3,
  input  in_4,
  input  [1:0] in_5,
  output out_6
);

  wire decoder_1_out0, decoder_1_out1, decoder_1_out2, decoder_1_out3;

  assign out_6 = decoder_1_out0 ? in_1 : 1'bz;  // Controlled_Buffer controlled_buffer_1
  assign out_6 = decoder_1_out1 ? in_2 : 1'bz;  // Controlled_Buffer controlled_buffer_2
  assign out_6 = decoder_1_out2 ? in_3 : 1'bz;  // Controlled_Buffer controlled_buffer_3
  Decoder #(.select(2), .enable("false")) decoder_1 (
    .out0(decoder_1_out0), .out1(decoder_1_out1), .out2(decoder_1_out2), .out3(decoder_1_out3), .sel(in_5));
  assign out_6 = decoder_1_out3 ? in_4 : 1'bz;  // Controlled_Buffer controlled_buffer_4
endmodule

module dcd_4bit (
  input  [3:0] in_1,
  output out_2,
  output out_3,
  output out_4,
  output out_5,
  output out_6,
  output out_7,
  output out_8,
  output out_9,
  output out_10,
  output out_11,
  output out_12,
  output out_13,
  output out_14,
  output out_15
);

  wire not_1_out, not_2_out, not_3_out, not_4_out;

  not not_1 (not_1_out, in_1[3]);
  not not_2 (not_2_out, in_1[2]);
  not not_3 (not_3_out, in_1[1]);
  not not_4 (not_4_out, in_1[0]);
  and and_1 (out_2, not_4_out, not_3_out, not_2_out, not_1_out);
  and and_2 (out_3, in_1[0], not_3_out, not_2_out, not_1_out);
  and and_3 (out_4, not_4_out, in_1[1], not_2_out, not_1_out);
  and and_4 (out_5, in_1[0], in_1[1], not_2_out, not_1_out);
  and and_5 (out_6, not_4_out, not_3_out, in_1[2], not_1_out);
  and and_6 (out_7, in_1[0], not_3_out, in_1[2], not_1_out);
  and and_7 (out_8, in_1[0], in_1[1], in_1[2], not_1_out);
  and and_8 (out_9, not_4_out, not_3_out, not_2_out, in_1[3]);
  and and_9 (out_10, in_1[0], not_3_out, not_2_out, in_1[3]);
  and and_10 (out_11, not_4_out, in_1[1], not_2_out, in_1[3]);
  and and_11 (out_12, in_1[0], in_1[1], not_2_out, in_1[3]);
  and and_12 (out_13, not_4_out, not_3_out, in_1[2], in_1[3]);
  and and_13 (out_14, in_1[0], not_3_out, in_1[2], in_1[3]);
  and and_14 (out_15, in_1[0], in_1[1], in_1[2], in_1[3]);
endmodule

module rotl (
  input  [7:0] A,
  output [7:0] out_2,
  output COUT
);


  assign COUT = A[7];
  assign out_2 = {A[6:0], A[7]};

  // Notes on the sheet:
  //   OUT
endmodule

module rotr (
  input  [7:0] A,
  output COUT,
  output [7:0] out_3
);


  assign COUT = A[0];
  assign out_3 = {A[0], A[7:1]};

  // Notes on the sheet:
  //   OUT
endmodule
