// Logisim project SR_latch.circ as structural Verilog: 1 circuit, main circuit main
module main (
  input  RESET,
  input  SET,
  input  RESET_2,
  input  SET_2,
  input  RESET_3,
  input  ENABLE,
  input  SET_3,
  output Q,
  output nQ,
  output Q_2,
  output nQ_2,
  output Q_3,
  output nQ_3
);

  wire and_1_out, and_2_out, and_3_out, nor_2_out;

  and and_1 (and_1_out, ~RESET, Q);  // AND_Gate
  nor nor_1 (Q_2, RESET_2, nor_2_out);
  or or_1 (Q, and_1_out, SET);
  not not_1 (nQ, Q);
  nor nor_2 (nor_2_out, Q_2, SET_2);
  and and_2 (and_2_out, RESET_3, ENABLE);
  and and_3 (and_3_out, ENABLE, SET_3);
  not not_2 (nQ_2, Q_2);
  nor nor_3 (Q_3, and_2_out, nQ_3);
  nor nor_4 (nQ_3, Q_3, and_3_out);
endmodule
