// Logisim project comp.circ as structural Verilog: 2 circuits, main circuit main
module main (
  input  [7:0] in_1,
  input  [7:0] in_2,
  output out_3,
  output [7:0] out_4
);

  wire comp_out_3, comp_out_4, comp_out_5;

  Adder adder_1 (.a(in_1), .b(in_2), .out(out_4));  // open: cin, cout
  comparator comp (.out_3(comp_out_3), .out_4(comp_out_4), .out_5(comp_out_5));  // open: in_1, in_2
endmodule

module comparator (
  input  [1:0] in_1,
  input  [1:0] in_2,
  output out_3,
  output out_4,
  output out_5
);

  wire and_1_out, and_2_out, and_3_out, not_1_out, not_2_out, xnor_1_out, xnor_2_out;

  not not_1 (not_1_out, in_2[1]);
  not not_2 (not_2_out, in_2[0]);
  and and_1 (and_1_out, in_1[1], not_1_out);
  and and_2 (and_2_out, in_1[1], in_1[0], not_2_out);
  and and_3 (and_3_out, in_1[0], not_1_out, not_2_out);
  xnor xnor_1 (xnor_1_out, in_1[1], in_2[1]);
  and and_4 (out_4, xnor_1_out, xnor_2_out);
  xnor xnor_2 (xnor_2_out, in_1[0], in_2[0]);
  or or_1 (out_3, and_1_out, and_2_out, and_3_out);
  nor nor_1 (out_5, out_3, out_4);
endmodule
