// Logisim project cpu.circ as structural Verilog: 1 circuit, main circuit main
module main (
  input  [7:0] in_1,
  input  in_2,
  input  in_3,
  input  in_4
);

  wire clock_1_out, decoder_1_out0, decoder_1_out1, decoder_1_out2, decoder_1_out3, decoder_1_out4,
       decoder_1_out5, decoder_1_out6, decoder_1_out7, decoder_1_out8, decoder_1_out9, decoder_1_out10,
       decoder_1_out11, decoder_1_out12, decoder_1_out13, decoder_1_out14, decoder_1_out15, set, set_a,
       set_b, set_bjh, set_bjl, set_brh, set_brl, set_c, set_d, set_e, set_f, set_jh, set_jl, set_k, set_l,
       set_rh, set_rl;
  wire [3:0] register_3_q, rom_1_data, rom_1_data_2, rom_1_data_3, rom_1_data_4;
  wire [7:0] register_1_q, register_2_q, register_5_q, register_6_q, register_7_q, register_8_q, undriven;

  Adder adder_1 ();  // open: a, b, out, cin, cout
  and and_1 (set_a, decoder_1_out0, set);
  and and_2 (set_b, decoder_1_out1, set);
  and and_3 (set_c, decoder_1_out2, set);
  and and_4 (set_d, decoder_1_out3, set);
  and and_5 (set_e, decoder_1_out4, set);
  and and_6 (set_f, decoder_1_out5, set);
  and and_7 (set_k, decoder_1_out6, set);
  and and_8 (set_l, decoder_1_out7, set);
  and and_9 (set_rh, decoder_1_out8, set);
  and and_10 (set_rl, decoder_1_out9, set);
  and and_11 (set_brh, decoder_1_out10, set);
  and and_12 (set_brl, decoder_1_out11, set);
  and and_13 (set_jh, decoder_1_out12, set);
  and and_14 (set_jl, decoder_1_out13, set);
  and and_15 (set_bjh, decoder_1_out14, set);
  and and_16 (set_bjl, decoder_1_out15, set);
  Register register_1 (.Q(register_1_q));  // open: D, en, clk, clr
  Register register_2 (.Q(register_2_q));  // open: D, en, clk, clr
  Decoder #(.select(4)) decoder_1 (
    .out0(decoder_1_out0), .out1(decoder_1_out1), .out2(decoder_1_out2), .out3(decoder_1_out3),
    .out4(decoder_1_out4), .out5(decoder_1_out5), .out6(decoder_1_out6), .out7(decoder_1_out7),
    .out8(decoder_1_out8), .out9(decoder_1_out9), .out10(decoder_1_out10), .out11(decoder_1_out11),
    .out12(decoder_1_out12), .out13(decoder_1_out13), .out14(decoder_1_out14), .out15(decoder_1_out15),
    .sel(rom_1_data_3));  // open: en
  ROM #(.addrWidth(16), .dataWidth(16)) rom_1 (
    .addr({register_2_q, register_1_q}), .data({rom_1_data_4, rom_1_data_3, rom_1_data_2, rom_1_data}),
    .sel(1'b1));
  // Probe on {rom_1_data_4, rom_1_data_3, rom_1_data_2, rom_1_data}
  Register #(.width(4)) register_3 (
    .D(rom_1_data_4), .en(clock_1_out), .Q(register_3_q), .clk(clock_1_out));  // open: clr
  Decoder #(.select(4), .enable("false")) decoder_2 (
    .out1(set), .sel(register_3_q));  // open: out0, out2, out3, out4, out5, out6, out7, out8, out9, out10, out11, out12, out13, out14, out15
  Clock clock_1 (.out(clock_1_out));
  Register register_4 (.D(in_1), .en(in_2), .clk(in_3), .clr(in_4));  // open: Q
  Controlled_Buffer #(.width(8)) controlled_buffer_1 (.in(register_5_q));  // open: out, en
  Register register_5 (.Q(register_5_q), .clk(set_a));  // open: D, en, clr
  Controlled_Buffer #(.width(8)) controlled_buffer_2 (.in(register_6_q));  // open: out, en
  Register register_6 (.Q(register_6_q));  // open: D, en, clk, clr
  Register register_7 (.Q(register_7_q));  // open: D, en, clk, clr
  Controlled_Buffer #(.width(8)) controlled_buffer_3 (.in(register_7_q));  // open: out, en
  Controlled_Buffer #(.width(8)) controlled_buffer_4 (.in(register_8_q));  // open: out, en
  Register register_8 (.Q(register_8_q));  // open: D, en, clk, clr
  RAM ram_1 ();  // open: addr, data, sel, clk, ld, clr
  Register register_9 (.D(undriven), .clk(set_b));  // open: en, Q, clr
  Register register_10 ();  // open: D, en, Q, clk, clr
  Register register_11 ();  // open: D, en, Q, clk, clr
  Register register_12 ();  // open: D, en, Q, clk, clr

  // Notes on the sheet:
  //   contents of rom_1 (hex, n*v repeats v):
  //   1120
endmodule
