// Logisim project smth.circ as structural Verilog: 2 circuits, main circuit main
module main (
  input  in_1
);
endmodule

module odcitacka (
  input  in_1,
  input  in_2,
  input  in_3,
  input  in_4,
  input  [3:0] in_5
);

  wire controlled_buffer_1_out, undriven, undriven_2;

  Demultiplexer #(.select(4)) demultiplexer_1 ();  // open: out0, out1, out2, out3, out4, out5, out6, out7, out8, out9, out10, out11, out12, out13, out14, out15, in, sel, en
  assign controlled_buffer_1_out = in_2 ? in_1 : 1'bz;  // Controlled_Buffer controlled_buffer_1
  Multiplexer multiplexer_1 (.in0(in_2), .in1(in_2), .sel(undriven), .en(undriven_2));  // open: out
  Decoder #(.select(4), .disabled(0)) decoder_1 (
    .sel(in_5), .en(in_4));  // open: out0, out1, out2, out3, out4, out5, out6, out7, out8, out9, out10, out11, out12, out13, out14, out15
endmodule
