// Logisim project cpu.circ as structural Verilog: 19 circuits, main circuit main
module main (
  input  [3:0] in_1,
  input  in_2,
  output [7:0] out_3
);

  wire alu_8_bit_1_p6, alu_8_bit_1_p7;
  wire [7:0] register_1_q, register_2_q;

  Register register_1 (.Q(register_1_q));  // open: D, en, clk, clr
  Register register_2 (.Q(register_2_q));  // open: D, en, clk, clr
  // ALU___8_bit alu_8_bit_1: pin names not known; wires that end beside it: register_1_q, register_2_q, in_2, in_1, out_3, alu_8_bit_1_p6, alu_8_bit_1_p7
  Hex_Digit_Display hex_digit_display_1 (.value(out_3[7:4]));  // open: dp
  LED led_1 (.in(alu_8_bit_1_p6));
  LED led_2 (.in(alu_8_bit_1_p7));
  Hex_Digit_Display hex_digit_display_2 (.value(out_3[3:0]));  // open: dp
endmodule

module adder1 (
  input  A,
  input  B,
  output X,
  output Cout
);

  xor xor_1 (X, A, B);
  and and_1 (Cout, A, B);
endmodule

module full_adder (
  input  Cin,
  input  A,
  input  B,
  output X,
  output Cout
);

  wire adder1_1_cout, adder1_1_x, adder1_2_cout;

  adder1 adder1_1 (.A(A), .B(B), .X(adder1_1_x), .Cout(adder1_1_cout));
  Pull_Resistor pull_resistor_1 (.node(Cin));
  adder1 adder1_2 (.A(adder1_1_x), .B(Cin), .X(X), .Cout(adder1_2_cout));
  or or_1 (Cout, adder1_2_cout, adder1_1_cout);
endmodule

module adder8 (
  input  [7:0] in_1,
  input  [7:0] in_2,
  input  Cin,
  output [7:0] out_4,
  output Cout
);

  wire full_adder_1_cout, full_adder_2_cout, full_adder_3_cout, full_adder_4_cout, full_adder_5_cout,
       full_adder_6_cout, full_adder_7_cout;

  Pull_Resistor pull_resistor_1 (.node(in_2));
  Pull_Resistor pull_resistor_2 (.node(Cin));
  full_adder full_adder_1 (.A(in_1[0]), .B(in_2[0]), .X(out_4[0]), .Cin(Cin), .Cout(full_adder_1_cout));
  full_adder full_adder_2 (.A(in_1[1]), .B(in_2[1]), .X(out_4[1]), .Cin(full_adder_1_cout), .Cout(full_adder_2_cout));
  full_adder full_adder_3 (.A(in_1[2]), .B(in_2[2]), .X(out_4[2]), .Cin(full_adder_2_cout), .Cout(full_adder_3_cout));
  full_adder full_adder_4 (.A(in_1[3]), .B(in_2[3]), .X(out_4[3]), .Cin(full_adder_3_cout), .Cout(full_adder_4_cout));
  full_adder full_adder_5 (.A(in_1[4]), .B(in_2[4]), .X(out_4[4]), .Cin(full_adder_4_cout), .Cout(full_adder_5_cout));
  full_adder full_adder_6 (.A(in_1[5]), .B(in_2[5]), .X(out_4[5]), .Cin(full_adder_5_cout), .Cout(full_adder_6_cout));
  full_adder full_adder_7 (.A(in_1[6]), .B(in_2[6]), .X(out_4[6]), .Cin(full_adder_6_cout), .Cout(full_adder_7_cout));
  full_adder full_adder_8 (.A(in_1[7]), .B(in_2[7]), .X(out_4[7]), .Cin(full_adder_7_cout), .Cout(Cout));

  // Notes on the sheet:
  //   X
endmodule

module ALU___8_bit (
  input  [7:0] A,
  input  [7:0] B,
  input  CIN,
  input  [3:0] SEL,
  output [7:0] OUT,
  output ZERO,
  output COUT
);

  wire ADD, addsub8_1_cout, AND, DEC, INC, NOT, OR, or_1_out, or_2_out, or_4_out, ROTL, rotl_1_cout, ROTR,
       rotr_1_cout, SHL, shl_1_cout, SHR, shr_1_cout, SUB, XOR;
  wire [7:0] addsub8_1_out_5, and_1_out, multiplexer_1_out, not_1_out, or_3_out, rotl_1_out_2, rotr_1_out_3,
       shl_1_out_3, shr_1_out_4, xor_1_out;

  instruction instruction_1 (
    .in_1(SEL), .XOR(XOR), .OR(OR), .AND(AND), .NOT(NOT), .SHL(SHL), .SHR(SHR), .ROTL(ROTL), .ROTR(ROTR),
    .ADD(ADD), .SUB(SUB), .INC(INC), .DEC(DEC));  // open: MUL
  Pull_Resistor pull_resistor_1 (.node(CIN));
  Multiplexer #(.width(8), .enable("false")) multiplexer_1 (
    .in0(B), .in1(8'h1), .out(multiplexer_1_out), .sel(or_2_out));
  or or_1 (or_1_out, SUB, DEC);
  or or_2 (or_2_out, DEC, INC);
  assign xor_1_out = A ^ B;  // XOR_Gate xor_1, 8 bits wide
  assign or_3_out = A | B;  // OR_Gate or_3, 8 bits wide
  assign and_1_out = A & B;  // AND_Gate and_1, 8 bits wide
  assign not_1_out = ~A;  // NOT_Gate not_1, 8 bits wide
  SHL shl_1 (.A(A), .out_3(shl_1_out_3), .COUT(shl_1_cout), .CIN(CIN));
  SHR shr_1 (.A(A), .COUT(shr_1_cout), .out_4(shr_1_out_4), .CIN(CIN));
  rotl rotl_1 (.A(A), .out_2(rotl_1_out_2), .COUT(rotl_1_cout));
  rotr rotr_1 (.A(A), .COUT(rotr_1_cout), .out_3(rotr_1_out_3));
  addSub8 addsub8_1 (
    .in_3(A), .in_4(multiplexer_1_out), .SUB(or_1_out), .out_5(addsub8_1_out_5), .COUT(addsub8_1_cout),
    .CIN(CIN));
  assign COUT = SHL ? shl_1_cout : 1'bz;  // Controlled_Buffer controlled_buffer_1
  assign COUT = SHR ? shr_1_cout : 1'bz;  // Controlled_Buffer controlled_buffer_2
  assign COUT = ROTL ? rotl_1_cout : 1'bz;  // Controlled_Buffer controlled_buffer_3
  assign COUT = ROTR ? rotr_1_cout : 1'bz;  // Controlled_Buffer controlled_buffer_4
  or or_4 (or_4_out, ADD, or_1_out, or_2_out);
  assign OUT = or_4_out ? addsub8_1_out_5 : 8'bz;  // Controlled_Buffer controlled_buffer_5
  assign COUT = or_4_out ? addsub8_1_cout : 1'bz;  // Controlled_Buffer controlled_buffer_6
  assign OUT = XOR ? xor_1_out : 8'bz;  // Controlled_Buffer controlled_buffer_7
  assign OUT = OR ? or_3_out : 8'bz;  // Controlled_Buffer controlled_buffer_8
  assign OUT = AND ? and_1_out : 8'bz;  // Controlled_Buffer controlled_buffer_9
  assign OUT = NOT ? not_1_out : 8'bz;  // Controlled_Buffer controlled_buffer_10
  assign OUT = SHL ? shl_1_out_3 : 8'bz;  // Controlled_Buffer controlled_buffer_11
  assign OUT = SHR ? shr_1_out_4 : 8'bz;  // Controlled_Buffer controlled_buffer_12
  assign OUT = ROTL ? rotl_1_out_2 : 8'bz;  // Controlled_Buffer controlled_buffer_13
  assign OUT = ROTR ? rotr_1_out_3 : 8'bz;  // Controlled_Buffer controlled_buffer_14
  nor nor_1 (ZERO, OUT[0], OUT[1], OUT[2], OUT[3], OUT[4], OUT[5], OUT[6], OUT[7]);
endmodule

module SHR (
  input  [7:0] A,
  input  CIN,
  output COUT,
  output [7:0] out_4
);

  Pull_Resistor pull_resistor_1 (.node(CIN));

  assign COUT = A[0];
  assign out_4 = {CIN, A[7:1]};

  // Notes on the sheet:
  //   OUT
endmodule

module SHL (
  input  CIN,
  input  [7:0] A,
  output [7:0] out_3,
  output COUT
);

  Pull_Resistor pull_resistor_1 (.node(CIN));

  assign COUT = A[7];
  assign out_3 = {A[6:0], CIN};

  // Notes on the sheet:
  //   OUT
endmodule

module instruction (
  input  [3:0] in_1,
  output XOR,
  output OR,
  output AND,
  output NOT,
  output SHL,
  output SHR,
  output ROTL,
  output ROTR,
  output ADD,
  output SUB,
  output INC,
  output DEC,
  output MUL
);

  and and_1 (XOR, ~in_1[0], ~in_1[1], ~in_1[2], ~in_1[3]);  // AND_Gate
  and and_2 (OR, in_1[0], ~in_1[1], ~in_1[2], ~in_1[3]);  // AND_Gate
  and and_3 (AND, ~in_1[0], in_1[1], ~in_1[2], ~in_1[3]);  // AND_Gate
  and and_4 (NOT, in_1[0], in_1[1], ~in_1[2], ~in_1[3]);  // AND_Gate
  and and_5 (SHL, ~in_1[0], ~in_1[1], in_1[2], ~in_1[3]);  // AND_Gate
  and and_6 (SHR, in_1[0], ~in_1[1], in_1[2], ~in_1[3]);  // AND_Gate
  and and_7 (ROTL, ~in_1[0], in_1[1], in_1[2], ~in_1[3]);  // AND_Gate
  and and_8 (ROTR, in_1[0], in_1[1], in_1[2], ~in_1[3]);  // AND_Gate
  and and_9 (ADD, ~in_1[0], ~in_1[1], ~in_1[2], in_1[3]);  // AND_Gate
  and and_10 (SUB, in_1[0], ~in_1[1], ~in_1[2], in_1[3]);  // AND_Gate
  and and_11 (INC, ~in_1[0], in_1[1], ~in_1[2], in_1[3]);  // AND_Gate
  and and_12 (DEC, in_1[0], in_1[1], ~in_1[2], in_1[3]);  // AND_Gate
  and and_13 (MUL, ~in_1[0], ~in_1[1], in_1[2], in_1[3]);  // AND_Gate
endmodule

module addSub8 (
  input  SUB,
  input  CIN,
  input  [7:0] in_3,
  input  [7:0] in_4,
  output [7:0] out_5,
  output COUT
);

  wire or_1_out;
  wire [7:0] xor_1_out;

  assign xor_1_out = {8{SUB}} ^ in_4;  // XOR_Gate xor_1, 8 bits wide
  or or_1 (or_1_out, CIN, SUB);
  adder8 adder8_1 (.in_1(in_3), .in_2(xor_1_out), .out_4(out_5), .Cin(or_1_out), .Cout(COUT));

  // Notes on the sheet:
  //   A
  //   B
  //   X
endmodule

module mul8 (
  input  [7:0] in_1,
  input  [7:0] in_2,
  output [7:0] out_3
);

  wire and_2_out, and_3_out, and_4_out, and_5_out, and_6_out, and_7_out, and_11_out, and_12_out, and_13_out,
       and_14_out, and_15_out, and_18_out, and_19_out, and_20_out, and_21_out, and_22_out, and_23_out,
       and_24_out, and_25_out, and_26_out, and_27_out, and_28_out, and_29_out, and_30_out, and_31_out,
       and_32_out, and_33_out, and_34_out, and_35_out, and_36_out, full_adder_1_cout, full_adder_2_cout,
       full_adder_2_x;

  and and_1 (out_3[0], in_2[0], in_1[0]);
  and and_2 (and_2_out, in_2[0], in_1[1]);
  and and_3 (and_3_out, in_2[1], in_1[0]);
  and and_4 (and_4_out, in_2[0], in_1[2]);
  and and_5 (and_5_out, in_2[1], in_1[1]);
  and and_6 (and_6_out, in_2[2], in_1[0]);
  and and_7 (and_7_out, in_2[0], in_1[3]);
  // AND_Gate and_8 has open pins: in0=in_2[1], in1=in_1[2], out=open
  // AND_Gate and_9 has open pins: in0=in_2[2], in1=in_1[1], out=open
  // AND_Gate and_10 has open pins: in0=in_2[3], in1=in_1[0], out=open
  and and_11 (and_11_out, in_2[0], in_1[4]);
  and and_12 (and_12_out, in_2[1], in_1[3]);
  and and_13 (and_13_out, in_2[2], in_1[2]);
  and and_14 (and_14_out, in_2[3], in_1[1]);
  and and_15 (and_15_out, in_2[4], in_1[0]);
  // AND_Gate and_16 has open pins: in0=in_2[0], in1=in_1[5], out=open
  // AND_Gate and_17 has open pins: in0=in_2[1], in1=in_1[4], out=open
  and and_18 (and_18_out, in_2[2], in_1[3]);
  and and_19 (and_19_out, in_2[3], in_1[2]);
  and and_20 (and_20_out, in_2[4], in_1[1]);
  and and_21 (and_21_out, in_2[5], in_1[0]);
  and and_22 (and_22_out, in_2[0], in_1[6]);
  and and_23 (and_23_out, in_2[1], in_1[5]);
  and and_24 (and_24_out, in_2[2], in_1[4]);
  and and_25 (and_25_out, in_2[3], in_1[3]);
  and and_26 (and_26_out, in_2[4], in_1[2]);
  and and_27 (and_27_out, in_2[5], in_1[1]);
  and and_28 (and_28_out, in_2[6], in_1[0]);
  and and_29 (and_29_out, in_2[0], in_1[7]);
  and and_30 (and_30_out, in_2[1], in_1[6]);
  and and_31 (and_31_out, in_2[2], in_1[5]);
  and and_32 (and_32_out, in_2[3], in_1[4]);
  and and_33 (and_33_out, in_2[4], in_1[3]);
  and and_34 (and_34_out, in_2[5], in_1[2]);
  and and_35 (and_35_out, in_2[6], in_1[1]);
  and and_36 (and_36_out, in_2[7], in_1[0]);
  // AND_Gate and_37 is placed but not wired
  // AND_Gate and_38 is placed but not wired
  // AND_Gate and_39 is placed but not wired
  // AND_Gate and_40 is placed but not wired
  // AND_Gate and_41 is placed but not wired
  // AND_Gate and_42 is placed but not wired
  full_adder full_adder_1 (.A(and_2_out), .B(and_3_out), .X(out_3[1]), .Cout(full_adder_1_cout));  // open: Cin
  full_adder full_adder_2 (
    .A(and_4_out), .B(and_5_out), .X(full_adder_2_x), .Cin(full_adder_1_cout), .Cout(full_adder_2_cout));
  full_adder full_adder_3 (.A(full_adder_2_x), .B(and_6_out), .X(out_3[2]), .Cin(full_adder_2_cout));  // open: Cout
  // OR_Gate or_1 has open pins: out=out_3[6]
endmodule

module mux (
  input  in_1,
  input  in_2,
  input  in_3,
  input  in_4,
  input  [1:0] in_5,
  output out_6
);

  wire decoder_1_out0, decoder_1_out1, decoder_1_out2, decoder_1_out3;

  assign out_6 = decoder_1_out0 ? in_1 : 1'bz;  // Controlled_Buffer controlled_buffer_1
  assign out_6 = decoder_1_out1 ? in_2 : 1'bz;  // Controlled_Buffer controlled_buffer_2
  assign out_6 = decoder_1_out2 ? in_3 : 1'bz;  // Controlled_Buffer controlled_buffer_3
  Decoder #(.select(2), .enable("false")) decoder_1 (
    .out0(decoder_1_out0), .out1(decoder_1_out1), .out2(decoder_1_out2), .out3(decoder_1_out3), .sel(in_5));
  assign out_6 = decoder_1_out3 ? in_4 : 1'bz;  // Controlled_Buffer controlled_buffer_4
endmodule

module dcd_4bit (
  input  [3:0] in_1,
  output out_2,
  output out_3,
  output out_4,
  output out_5,
  output out_6,
  output out_7,
  output out_8,
  output out_9,
  output out_10,
  output out_11,
  output out_12,
  output out_13,
  output out_14,
  output out_15
);

  wire not_1_out, not_2_out, not_3_out, not_4_out;

  not not_1 (not_1_out, in_1[3]);
  not not_2 (not_2_out, in_1[2]);
  not not_3 (not_3_out, in_1[0]);
  not not_4 (not_4_out, in_1[1]);
  and and_1 (out_2, not_3_out, not_4_out, not_2_out, not_1_out);
  and and_2 (out_3, in_1[0], not_4_out, not_2_out, not_1_out);
  and and_3 (out_4, not_3_out, in_1[1], not_2_out, not_1_out);
  and and_4 (out_5, in_1[0], in_1[1], not_2_out, not_1_out);
  and and_5 (out_6, not_3_out, not_4_out, in_1[2], not_1_out);
  and and_6 (out_7, in_1[0], not_4_out, in_1[2], not_1_out);
  and and_7 (out_8, in_1[0], in_1[1], in_1[2], not_1_out);
  and and_8 (out_9, not_3_out, not_4_out, not_2_out, in_1[3]);
  and and_9 (out_10, in_1[0], not_4_out, not_2_out, in_1[3]);
  and and_10 (out_11, not_3_out, in_1[1], not_2_out, in_1[3]);
  and and_11 (out_12, in_1[0], in_1[1], not_2_out, in_1[3]);
  and and_12 (out_13, not_3_out, not_4_out, in_1[2], in_1[3]);
  and and_13 (out_14, in_1[0], not_4_out, in_1[2], in_1[3]);
  and and_14 (out_15, in_1[0], in_1[1], in_1[2], in_1[3]);
endmodule

module rotl (
  input  [7:0] A,
  output [7:0] out_2,
  output COUT
);


  assign COUT = A[7];
  assign out_2 = {A[6:0], A[7]};

  // Notes on the sheet:
  //   OUT
endmodule

module rotr (
  input  [7:0] A,
  output COUT,
  output [7:0] out_3
);


  assign COUT = A[0];
  assign out_3 = {A[0], A[7:1]};

  // Notes on the sheet:
  //   OUT
endmodule

module cpu (
  input  in_1,
  input  in_2
);

  wire _0, _1, _2, _3, _4, _5, _6, a_ena, a_set, alu, alu_8_bit_1_cout, alu_out_ena, and_1_out, and_2_out,
       and_19_out, and_20_out, and_25_out, and_26_out, b_ena, b_set, bjh_ena, bjh_set, bjl_ena, bjl_set,
       brh_ena, brh_set, brl_ena, brl_set, c_ena, c_set, clock_1_out, d_ena, d_set, e_ena, e_set, ena,
       ena_set_1_out_3, f_ena, f_set, hex_set, jh_ena, jh_set, jh_static_set, jh_static_set_jmp, jl_ena,
       jl_set, jl_static_set, jl_static_set_jmp, jmp, jmpi, k_ena, k_set, l0_set, l1_set, l2_set, l3_set,
       l4_set, l5_set, l6_set, l7_set, l_ena, l_set, ld, ld_ira, mov, movi, next_alu, next_jmp, next_ld,
       next_mov, next_movi, next_out, next_st, or_1_out, or_2_out, or_3_out, or_4_out, or_5_out, or_6_out,
       or_7_out, or_8_out, or_9_out, or_10_out, or_11_out, or_12_out, out, pc_ena, pc_inc, pc_set,
       pc_set_jmp, ram_ena, ram_ena_ld, ram_set, ram_set_st, reg_ena, reg_ena_alu_1, reg_ena_alu_2,
       reg_ena_mov, reg_ena_out, reg_ena_st, reg_set, reg_set_movi, rh_ena, rh_set, rl_ena, rl_set, rst, set,
       st, stepper_1_out_10, temp_a_set, temp_b_set, undefined, undefined2;
  wire [3:0] alu_op, arg1, arg2, arg3, ira, reg_ena_addr, reg_set_addr;
  wire [7:0] A_q, alu_8_bit_1_out, B_q, C_q, controlled_buffer_2_out, controlled_buffer_3_out, D_q,
       demultiplexer_2_out0, demultiplexer_2_out1, demultiplexer_3_out1, demultiplexer_4_out0,
       demultiplexer_4_out1, demultiplexer_4_out2, demultiplexer_4_out3, demultiplexer_4_out4,
       demultiplexer_4_out5, demultiplexer_4_out6, demultiplexer_4_out7, E_q, F_q, harvester_of_sorrow,
       harvester_of_sorrow_t, JH_2_q, JL_2_q, K_q, L_q, register_2_q, register_3_q, register_4_q,
       register_5_q, register_6_q, register_7_q, register_8_q, register_9_q, RH_q, RL_q, TEMP_A_q, TEMP_B_q,
       undriven, undriven_2;
  wire [15:0] adder_1_out, controlled_buffer_1_out, JL_q, multiplexer_1_out, register_1_q, rom_1_data;

  Demultiplexer #(.enable("false")) demultiplexer_1 (.in(in_1), .sel(in_2));  // open: out0, out1
  Register JH (.D(harvester_of_sorrow), .Q(JL_q[15:8]), .clk(jh_static_set), .clr(rst));  // open: en
  Register JL (.D(harvester_of_sorrow), .Q(JL_q[7:0]), .clk(jl_static_set), .clr(rst));  // open: en
  Multiplexer #(.width(16), .enable("false")) multiplexer_1 (
    .in0(JL_q), .in1(adder_1_out), .out(multiplexer_1_out), .sel(pc_inc));
  and and_1 (and_1_out, reg_set, set);
  and and_2 (and_2_out, reg_ena, ena);
  Register #(.width(16)) register_1 (.D(multiplexer_1_out), .Q(register_1_q), .clk(pc_set), .clr(rst));  // open: en
  Decoder #(.select(4), .enable("false")) decoder_1 (
    .out0(mov), .out1(st), .out2(ld), .out3(alu), .out4(jmp), .out5(movi), .out6(jmpi), .out15(out), .sel(ira));  // open: out7, out8, out9, out10, out11, out12, out13, out14
  Decoder #(.select(4)) decoder_2 (
    .out0(k_set), .out1(l_set), .out2(jl_set), .out3(jh_set), .out4(bjl_set), .out5(bjh_set), .out6(rl_set),
    .out7(rh_set), .out8(brl_set), .out9(brh_set), .out10(a_set), .out11(b_set), .out12(c_set),
    .out13(d_set), .out14(e_set), .out15(f_set), .sel(reg_set_addr), .en(and_1_out));
  Decoder #(.select(4)) decoder_3 (
    .out0(k_ena), .out1(l_ena), .out2(jl_ena), .out3(jh_ena), .out4(bjl_ena), .out5(bjh_ena), .out6(rl_ena),
    .out7(rh_ena), .out8(brl_ena), .out9(brh_ena), .out10(a_ena), .out11(b_ena), .out12(c_ena),
    .out13(d_ena), .out14(e_ena), .out15(f_ena), .sel(reg_ena_addr), .en(and_2_out));
  assign controlled_buffer_1_out = pc_ena ? register_1_q : 16'bz;  // Controlled_Buffer controlled_buffer_1
  Register JH_2 (.D(undriven), .Q(JH_2_q), .clk(jh_set), .clr(rst));  // open: en
  Register JL_2 (.D(undriven), .Q(JL_2_q), .clk(jl_set), .clr(rst));  // open: en
  Clock clock_1 (.out(clock_1_out));
  Pull_Resistor pull_resistor_1 (.node(k_set));
  Pull_Resistor pull_resistor_2 (.node(l_set));
  Pull_Resistor pull_resistor_3 (.node(jl_set));
  Pull_Resistor pull_resistor_4 (.node(jh_set));
  Pull_Resistor pull_resistor_5 (.node(bjl_set));
  Pull_Resistor pull_resistor_6 (.node(bjh_set));
  Pull_Resistor pull_resistor_7 (.node(rl_set));
  Pull_Resistor pull_resistor_8 (.node(rh_set));
  Pull_Resistor pull_resistor_9 (.node(brl_set));
  Pull_Resistor pull_resistor_10 (.node(brh_set));
  Pull_Resistor pull_resistor_11 (.node(a_set));
  Pull_Resistor pull_resistor_12 (.node(b_set));
  Pull_Resistor pull_resistor_13 (.node(c_set));
  Pull_Resistor pull_resistor_14 (.node(d_set));
  Pull_Resistor pull_resistor_15 (.node(e_set));
  Pull_Resistor pull_resistor_16 (.node(f_set));
  Pull_Resistor pull_resistor_17 (.node(k_ena));
  Pull_Resistor pull_resistor_18 (.node(l_ena));
  Pull_Resistor pull_resistor_19 (.node(jl_ena));
  Pull_Resistor pull_resistor_20 (.node(jh_ena));
  Pull_Resistor pull_resistor_21 (.node(bjl_ena));
  Pull_Resistor pull_resistor_22 (.node(bjh_ena));
  Pull_Resistor pull_resistor_23 (.node(rl_ena));
  Pull_Resistor pull_resistor_24 (.node(rh_ena));
  Pull_Resistor pull_resistor_25 (.node(brl_ena));
  Pull_Resistor pull_resistor_26 (.node(brh_ena));
  Pull_Resistor pull_resistor_27 (.node(a_ena));
  Pull_Resistor pull_resistor_28 (.node(b_ena));
  Pull_Resistor pull_resistor_29 (.node(c_ena));
  Pull_Resistor pull_resistor_30 (.node(d_ena));
  Pull_Resistor pull_resistor_31 (.node(e_ena));
  Pull_Resistor pull_resistor_32 (.node(f_ena));
  Adder #(.width(16)) adder_1 (.a(controlled_buffer_1_out), .b(16'h1), .out(adder_1_out));  // open: cin, cout
  assign controlled_buffer_2_out = jh_ena ? JH_2_q : 8'bz;  // Controlled_Buffer controlled_buffer_2
  Demultiplexer #(.width(8), .enable("false")) demultiplexer_2 (
    .out0(demultiplexer_2_out0), .out1(demultiplexer_2_out1), .in(controlled_buffer_2_out), .sel(jmp));
  Demultiplexer #(.width(8), .enable("false")) demultiplexer_3 (
    .out0(demultiplexer_2_out0), .out1(demultiplexer_3_out1), .in(controlled_buffer_3_out), .sel(jmp));
  assign controlled_buffer_3_out = jl_ena ? JL_2_q : 8'bz;  // Controlled_Buffer controlled_buffer_3
  ena_set ena_set_1 (.in_2(clock_1_out), .out_3(ena_set_1_out_3), .out_4(ena), .out_5(set));  // open: in_1
  Register JL_3 (.D(undriven_2));  // open: en, Q, clk, clr
  stepper stepper_1 (
    .CLK(ena_set_1_out_3), .RST(or_1_out), .out_3(_0), .out_7(_1), .out_4(_2), .out_8(_3), .out_5(_4),
    .out_9(_5), .out_6(_6), .out_10(stepper_1_out_10));
  ROM #(.addrWidth(16), .dataWidth(16)) rom_1 (.addr(controlled_buffer_1_out), .data(rom_1_data));  // open: sel
  or or_1 (or_1_out, next_mov, next_movi, next_st, next_ld, next_jmp, next_alu, next_out, stepper_1_out_10);
  and and_3 (pc_inc, _0, ~jmp);  // AND_Gate
  Register #(.width(4)) u_IRA (.D(rom_1_data[15:12]), .Q(ira), .clk(ld_ira));  // open: en, clr
  Register #(.width(4)) u_ARG1 (.D(rom_1_data[11:8]), .Q(arg1), .clk(ld_ira));  // open: en, clr
  Register #(.width(4)) u_ARG2 (.D(rom_1_data[7:4]), .Q(arg2), .clk(ld_ira));  // open: en, clr
  Register #(.width(4)) u_ARG3 (.D(rom_1_data[3:0]), .Q(arg3), .clk(ld_ira));  // open: en, clr
  or or_2 (or_2_out, reg_ena_st, ram_set_st, reg_ena_alu_1, reg_ena_alu_2, jl_static_set_jmp, jh_static_set_jmp, reg_ena_out, undefined, undefined, undefined);
  and and_4 (reg_ena, ena, or_2_out);
  and and_5 (ram_ena, ena, or_3_out);
  or or_3 (or_3_out, ram_ena_ld, undefined, undefined, undefined, undefined, undefined, undefined, undefined, undefined, undefined);
  and and_6 (pc_ena, ena, or_4_out);
  or or_4 (or_4_out, undefined, _0, undefined, undefined, undefined, undefined, undefined, undefined, undefined, undefined);
  or or_5 (or_5_out, undefined, undefined, undefined, undefined, undefined, undefined, undefined, undefined, undefined, undefined);
  and and_7 (undefined2, ena, or_5_out);
  Pull_Resistor pull_resistor_33 (.node(ram_ena_ld));
  assign harvester_of_sorrow = a_ena ? A_q : 8'bz;  // Controlled_Buffer controlled_buffer_4
  Register A (.D(harvester_of_sorrow), .Q(A_q), .clk(a_set), .clr(rst));  // open: en
  Register C (.D(harvester_of_sorrow), .Q(C_q), .clk(c_set), .clr(rst));  // open: en
  assign harvester_of_sorrow = c_ena ? C_q : 8'bz;  // Controlled_Buffer controlled_buffer_5
  Register E (.D(harvester_of_sorrow), .Q(E_q), .clk(e_set), .clr(rst));  // open: en
  assign harvester_of_sorrow = e_ena ? E_q : 8'bz;  // Controlled_Buffer controlled_buffer_6
  Register K (.D(harvester_of_sorrow), .Q(K_q), .clk(k_set), .clr(rst));  // open: en
  assign harvester_of_sorrow = k_ena ? K_q : 8'bz;  // Controlled_Buffer controlled_buffer_7
  Register B (.D(harvester_of_sorrow), .Q(B_q), .clk(b_set), .clr(rst));  // open: en
  Register D (.D(harvester_of_sorrow), .Q(D_q), .clk(d_set), .clr(rst));  // open: en
  Register F (.D(harvester_of_sorrow), .Q(F_q), .clk(f_set), .clr(rst));  // open: en
  Register L (.D(harvester_of_sorrow), .Q(L_q), .clk(l_set), .clr(rst));  // open: en
  and and_8 (ld_ira, set, _0);
  and and_9 (temp_a_set, set, reg_ena_alu_1);
  and and_10 (temp_b_set, set, reg_ena_alu_2);
  and and_11 (jl_static_set, set, jl_static_set_jmp);
  and and_12 (jh_static_set, set, jh_static_set_jmp);
  and and_13 (pc_set, set, or_10_out);
  Register RH (.D(harvester_of_sorrow), .Q(RH_q), .clk(rh_set), .clr(rst));  // open: en
  Register RL (.D(harvester_of_sorrow), .Q(RL_q), .clk(rl_set), .clr(rst));  // open: en
  assign harvester_of_sorrow = b_ena ? B_q : 8'bz;  // Controlled_Buffer controlled_buffer_8
  assign harvester_of_sorrow = d_ena ? D_q : 8'bz;  // Controlled_Buffer controlled_buffer_9
  assign harvester_of_sorrow = f_ena ? F_q : 8'bz;  // Controlled_Buffer controlled_buffer_10
  assign harvester_of_sorrow = l_ena ? L_q : 8'bz;  // Controlled_Buffer controlled_buffer_11
  or or_6 (or_6_out, reg_ena_st, ram_ena_ld, alu_out_ena, reg_set_movi, undefined, undefined, undefined, undefined, undefined, undefined);
  and and_14 (reg_set, set, or_6_out);
  or or_7 (or_7_out, ram_set_st, undefined, undefined, undefined, undefined, undefined, undefined, undefined, undefined, undefined);
  and and_15 (ram_set, set, or_7_out);
  and and_16 (undefined2, set, or_8_out);
  or or_8 (or_8_out, undefined, undefined, undefined, undefined, undefined, undefined, undefined, undefined, undefined, undefined);
  and and_17 (undefined2, set, or_9_out);
  or or_9 (or_9_out, undefined, undefined, undefined, undefined, undefined, undefined, undefined, undefined, undefined, undefined);
  or or_10 (or_10_out, pc_set_jmp, _0, undefined, undefined, undefined, undefined, undefined, undefined, undefined, undefined);
  Pull_Resistor pull_resistor_34 (.node(ram_set_st));
  Pull_Resistor pull_resistor_35 (.node(undefined));
  or or_11 (or_11_out, ram_set, ram_ena);
  RAM #(.addrWidth(16), .bus("asynch")) ram_1 (
    .addr({RH_q, RL_q}), .data(harvester_of_sorrow), .sel(or_11_out), .ld(ram_ena));  // open: clr
  Register TEMP_A (.D(harvester_of_sorrow), .Q(TEMP_A_q), .clk(temp_a_set), .clr(rst));  // open: en
  Register TEMP_B (.D(harvester_of_sorrow), .Q(TEMP_B_q), .clk(temp_b_set), .clr(rst));  // open: en
  // Probe on alu_op
  ALU___8_bit alu_8_bit_1 (
    .A(TEMP_A_q), .B(TEMP_B_q), .OUT(alu_8_bit_1_out), .COUT(alu_8_bit_1_cout), .SEL(alu_op));  // open: CIN, ZERO
  assign harvester_of_sorrow = alu_out_ena ? alu_8_bit_1_out : 8'bz;  // Controlled_Buffer controlled_buffer_12
  Pull_Resistor pull_resistor_36 (.node(alu_out_ena));
  and and_18 (reg_ena_mov, _1, mov);
  and and_19 (and_19_out, _1, st);
  and and_20 (and_20_out, _1, ld);
  and and_21 (reg_ena_alu_1, _1, alu);
  and and_22 (reg_set_movi, _1, movi);
  and and_23 (jl_static_set_jmp, _1, jmp);
  and and_24 (reg_ena_out, _1, out);
  assign reg_set_addr = reg_ena_mov ? arg1 : 4'bz;  // Controlled_Buffer controlled_buffer_13
  assign reg_ena_addr = reg_ena_mov ? arg2 : 4'bz;  // Controlled_Buffer controlled_buffer_14
  or or_12 (or_12_out, and_19_out, and_20_out);
  D_Flip_Flop CARRY (.D(alu_8_bit_1_cout));  // open: clk, Q, Qn, preset, en, reset
  assign reg_ena_addr = jl_static_set_jmp ? arg1 : 4'bz;  // Controlled_Buffer controlled_buffer_15
  assign reg_ena_addr = reg_ena_out ? arg1 : 4'bz;  // Controlled_Buffer controlled_buffer_16
  assign reg_ena_addr = or_12_out ? arg2 : 4'bz;  // Controlled_Buffer controlled_buffer_17
  assign reg_set_addr = or_12_out ? 4'b0110 : 4'bz;  // Controlled_Buffer controlled_buffer_18
  assign reg_ena_st = or_12_out ? or_12_out : 1'bz;  // Controlled_Buffer controlled_buffer_19
  assign reg_ena_st = or_12_out ? or_12_out : 1'bz;  // Controlled_Buffer controlled_buffer_20
  assign reg_ena_addr = reg_ena_alu_1 ? arg2 : 4'bz;  // Controlled_Buffer controlled_buffer_21
  assign reg_set_addr = reg_set_movi ? arg1 : 4'bz;  // Controlled_Buffer controlled_buffer_22
  assign harvester_of_sorrow_t[7:4] = reg_set_movi ? arg2 : 4'bz;  // Controlled_Buffer controlled_buffer_23
  assign harvester_of_sorrow_t[3:0] = reg_set_movi ? arg3 : 4'bz;  // Controlled_Buffer controlled_buffer_24
  not not_1 (hex_set, arg2[0]);
  and and_25 (and_25_out, _2, st);
  and and_26 (and_26_out, _2, ld);
  and and_27 (reg_ena_alu_2, _2, alu);
  and and_28 (next_mov, _2, mov);
  and and_29 (jh_static_set_jmp, _2, jmp);
  and and_30 (next_movi, _2, movi);
  and and_31 (next_out, _2, out);
  or or_13 (reg_ena_st, and_25_out, and_26_out);
  assign reg_ena_addr = reg_ena_st ? arg3 : 4'bz;  // Controlled_Buffer controlled_buffer_25
  assign reg_set_addr = reg_ena_st ? 4'b0111 : 4'bz;  // Controlled_Buffer controlled_buffer_26
  assign reg_ena_addr = reg_ena_alu_2 ? arg3 : 4'bz;  // Controlled_Buffer controlled_buffer_27
  assign reg_ena_addr = jh_static_set_jmp ? arg2 : 4'bz;  // Controlled_Buffer controlled_buffer_28
  and and_32 (ram_set_st, _3, st);
  and and_33 (ram_ena_ld, _3, ld);
  and and_34 (alu_out_ena, _3, alu);
  and and_35 (pc_set_jmp, _3, jmp);
  assign reg_ena_addr = ram_set_st ? arg1 : 4'bz;  // Controlled_Buffer controlled_buffer_29
  assign reg_set_addr = ram_ena_ld ? arg1 : 4'bz;  // Controlled_Buffer controlled_buffer_30
  assign alu_op = alu_out_ena ? arg1 : 4'bz;  // Controlled_Buffer controlled_buffer_31
  assign reg_set_addr = alu_out_ena ? arg2 : 4'bz;  // Controlled_Buffer controlled_buffer_32
  and and_36 (next_st, _4, st);
  and and_37 (next_ld, _4, ld);
  and and_38 (next_alu, _4, alu);
  and and_39 (next_jmp, _4, jmp);
  Decoder #(.select(3), .disabled(0)) decoder_4 (
    .out0(l0_set), .out1(l1_set), .out2(l2_set), .out3(l3_set), .out4(l4_set), .out5(l5_set), .out6(l6_set),
    .out7(l7_set), .sel(arg2[3:1]), .en(set));
  Demultiplexer #(.select(3), .width(8), .disabled(0), .enable("false")) demultiplexer_4 (
    .out0(demultiplexer_4_out0), .out1(demultiplexer_4_out1), .out2(demultiplexer_4_out2),
    .out3(demultiplexer_4_out3), .out4(demultiplexer_4_out4), .out5(demultiplexer_4_out5),
    .out6(demultiplexer_4_out6), .out7(demultiplexer_4_out7), .in(harvester_of_sorrow), .sel(arg2[3:1]));
  Register register_2 (.D(demultiplexer_4_out0), .Q(register_2_q), .clk(l0_set));  // open: en, clr
  Register register_3 (.D(demultiplexer_4_out1), .Q(register_3_q), .clk(l1_set));  // open: en, clr
  Register register_4 (.D(demultiplexer_4_out2), .Q(register_4_q), .clk(l2_set));  // open: en, clr
  Register register_5 (.D(demultiplexer_4_out3), .Q(register_5_q), .clk(l3_set));  // open: en, clr
  Register register_6 (.D(demultiplexer_4_out4), .Q(register_6_q), .clk(l4_set));  // open: en, clr
  Register register_7 (.D(demultiplexer_4_out5), .Q(register_7_q), .clk(l5_set));  // open: en, clr
  Register register_8 (.D(demultiplexer_4_out6), .Q(register_8_q), .clk(l6_set));  // open: en, clr
  Register register_9 (.D(demultiplexer_4_out7), .Q(register_9_q), .clk(l7_set));  // open: en, clr
  DotMatrix #(.matrixcols(8), .matrixrows(8)) dotmatrix_1 (
    .col0(register_2_q), .col1(register_3_q), .col2(register_4_q), .col3(register_5_q), .col4(register_6_q),
    .col5(register_7_q), .col6(register_8_q), .col7(register_9_q));

  // Other names for the same wires on the sheet: led_set = arg2[0]; l_block[2:0] = arg2[3:1]; ld_ira_start = _0;
  //   pc_ena_0 = _0; pc_set_0 = _0; reg_ena_jmp_1 = jl_static_set_jmp; reg_ena_jmp_2 = jh_static_set_jmp;
  //   reg_ena_st3 = ram_set_st; reg_set_alu = alu_out_ena; reg_set_ld = ram_ena_ld; reg_set_mov = reg_ena_mov;
  //   reg_set_st = reg_ena_st; temp_a_set_start = reg_ena_alu_1; temp_b_set_start = reg_ena_alu_2

  // Notes on the sheet:
  //   contents of rom_1 (hex, n*v repeats v):
  //   fa10 fb30 fc50
  //   Of Register and Man
  //   Master of Buffers
  //   Hit The Lights
endmodule

module stepper (
  input  CLK,
  input  RST,
  output out_3,
  output out_4,
  output out_5,
  output out_6,
  output out_7,
  output out_8,
  output out_9,
  output out_10
);

  wire [2:0] counter_1_q;

  Counter #(.width(3), .max('h7)) counter_1 (
    .count(1'b1), .Q(counter_1_q), .clk(CLK), .clr(RST));  // open: load, D, carry
  Decoder #(.select(3), .enable("false")) decoder_1 (
    .out0(out_3), .out1(out_7), .out2(out_4), .out3(out_8), .out4(out_5), .out5(out_9), .out6(out_6),
    .out7(out_10), .sel(counter_1_q));
endmodule

module ena_set (
  input  in_1,
  input  in_2,
  output out_3,
  output out_4,
  output out_5
);

  wire or_1_out, stepper_1_out_7, stepper_1_out_8, stepper_1_out_9;

  stepper stepper_1 (
    .CLK(in_2), .RST(or_1_out), .out_3(out_3), .out_7(stepper_1_out_7), .out_4(out_5),
    .out_8(stepper_1_out_8), .out_9(stepper_1_out_9));  // open: out_5, out_6, out_10
  or or_1 (or_1_out, in_1, stepper_1_out_9);
  or or_2 (out_4, stepper_1_out_7, out_5, stepper_1_out_8);
endmodule

module cb_lifehack (
  input  in_1,
  output out_2
);

  assign out_2 = in_1 ? in_1 : 1'bz;  // Controlled_Buffer controlled_buffer_1
endmodule

module adder16 (
  input  [15:0] in_1,
  input  [15:0] in_2,
  input  in_3,
  output [15:0] out_4,
  output out_5
);

  wire adder8_1_cout;

  Pull_Resistor pull_resistor_1 (.node(in_3));
  adder8 adder8_1 (.in_1(in_1[7:0]), .in_2(in_2[7:0]), .out_4(out_4[7:0]), .Cin(in_3), .Cout(adder8_1_cout));
  adder8 adder8_2 (.in_1(in_1[15:8]), .in_2(in_2[15:8]), .out_4(out_4[15:8]), .Cin(adder8_1_cout), .Cout(out_5));
endmodule
