// Logisim project 16_01_2023.circ as structural Verilog: 1 circuit, main circuit main
module main (
  input  RESET,
  input  SET,
  input  RESET_2,
  input  SET_2,
  output Q,
  output nQ
);

  wire and_1_out, clock_1_out, nor_1_out, nor_2_out, s_r_ff_1_q;

  Clock clock_1 (.out(clock_1_out));
  nor nor_1 (nor_1_out, RESET_2, nor_2_out);
  and and_1 (and_1_out, ~RESET, Q);  // AND_Gate
  or or_1 (Q, and_1_out, SET);
  nor nor_2 (nor_2_out, nor_1_out, SET_2);
  S_R_Flip_Flop s_r_ff_1 (.S(SET), .clk(clock_1_out), .R(RESET), .Q(s_r_ff_1_q));  // open: Qn, preset, reset, en
  not not_1 (nQ, Q);
endmodule
