// Logisim project 30_01_2023.circ as structural Verilog: 1 circuit, main circuit main
module main (
  input  in_1,
  input  in_2,
  output out_3
);

  wire d_ff_1_qn, not_1_out, not_2_out, not_3_out;

  not not_1 (not_1_out, in_1);
  D_Flip_Flop d_ff_1 (.clk(in_2), .D(d_ff_1_qn), .Qn(d_ff_1_qn));  // open: Q, preset, en, reset
  not not_2 (not_2_out, not_1_out);
  not not_3 (not_3_out, not_2_out);
  and and_1 (out_3, not_3_out, in_1);

  // Notes on the sheet:
  //   t flip flop (toogle)
  //   nepouzivat
endmodule
