// Logisim project adder.circ as structural Verilog: 5 circuits, main circuit main
module main (
);

  wire [7:0] adder8_1_out_4, register_1_q, register_2_q;

  Register register_1 (.Q(register_1_q));  // open: D, en, clk, clr
  Register register_2 (.Q(register_2_q));  // open: D, en, clk, clr
  adder8 adder8_1 (.in_1(register_1_q), .in_2(register_2_q), .out_4(adder8_1_out_4));  // open: Cin, Cout
  // Probe on adder8_1_out_4
endmodule

module adder1 (
  input  A,
  input  B,
  output X,
  output Cout
);

  xor xor_1 (X, A, B);
  and and_1 (Cout, A, B);
endmodule

module adder2 (
  input  [1:0] in_1,
  input  [1:0] in_2
);

  adder1 adder1_1 (.A(in_1[1]), .B(in_2[1]));  // open: X, Cout
endmodule

module full_adder (
  input  Cin,
  input  A,
  input  B,
  output X,
  output Cout
);

  wire adder1_1_cout, adder1_1_x, adder1_2_cout;

  adder1 adder1_1 (.A(A), .B(B), .X(adder1_1_x), .Cout(adder1_1_cout));
  Pull_Resistor pull_resistor_1 (.node(Cin));
  adder1 adder1_2 (.A(adder1_1_x), .B(Cin), .X(X), .Cout(adder1_2_cout));
  or or_1 (Cout, adder1_2_cout, adder1_1_cout);
endmodule

module adder8 (
  input  [7:0] in_1,
  input  [7:0] in_2,
  input  Cin,
  output [7:0] out_4,
  output Cout
);

  wire full_adder_1_cout, full_adder_2_cout, full_adder_3_cout, full_adder_4_cout, full_adder_5_cout,
       full_adder_6_cout, full_adder_7_cout;

  Pull_Resistor pull_resistor_1 (.node(Cin));
  full_adder full_adder_1 (.A(in_1[0]), .B(in_2[0]), .X(out_4[0]), .Cin(Cin), .Cout(full_adder_1_cout));
  full_adder full_adder_2 (.A(in_1[1]), .B(in_2[1]), .X(out_4[1]), .Cin(full_adder_1_cout), .Cout(full_adder_2_cout));
  full_adder full_adder_3 (.A(in_1[2]), .B(in_2[2]), .X(out_4[2]), .Cin(full_adder_2_cout), .Cout(full_adder_3_cout));
  full_adder full_adder_4 (.A(in_1[3]), .B(in_2[3]), .X(out_4[3]), .Cin(full_adder_3_cout), .Cout(full_adder_4_cout));
  full_adder full_adder_5 (.A(in_1[4]), .B(in_2[4]), .X(out_4[4]), .Cin(full_adder_4_cout), .Cout(full_adder_5_cout));
  full_adder full_adder_6 (.A(in_1[5]), .B(in_2[5]), .X(out_4[5]), .Cin(full_adder_5_cout), .Cout(full_adder_6_cout));
  full_adder full_adder_7 (.A(in_1[6]), .B(in_2[6]), .X(out_4[6]), .Cin(full_adder_6_cout), .Cout(full_adder_7_cout));
  full_adder full_adder_8 (.A(in_1[7]), .B(in_2[7]), .X(out_4[7]), .Cin(full_adder_7_cout), .Cout(Cout));

  // Notes on the sheet:
  //   X
endmodule
