// Logisim project comperator.circ as structural Verilog: 7 circuits, main circuit main
module main (
);

  wire comp32_1_a____b, comp32_1_a___b, comp32_1_a___b_2;
  wire [31:0] A_q, B_q;

  Register #(.width(32)) A (.Q(A_q));  // open: D, en, clk, clr
  Register #(.width(32)) B (.Q(B_q));  // open: D, en, clk, clr
  LED led_1 (.in(comp32_1_a___b));
  comp32 comp32_1 (.A(A_q), .B(B_q), .A___B(comp32_1_a___b), .A____B(comp32_1_a____b), .A___B_2(comp32_1_a___b_2));
  LED led_2 (.in(comp32_1_a____b));
  LED led_3 (.in(comp32_1_a___b_2));
endmodule

module comp (
  input  A,
  input  B,
  output A_B,
  output A__B,
  output A_B_2
);

  and and_1 (A_B, ~A, B);  // AND_Gate
  xnor xnor_1 (A__B, A, B);
  and and_2 (A_B_2, A, ~B);  // AND_Gate
endmodule

module comp2 (
  input  [1:0] A,
  input  [1:0] B,
  output A___B,
  output A____B,
  output A___B_2
);

  wire and_1_out, comp_1_a__b, comp_1_a_b, comp_2_a__b, comp_2_a_b;

  comp comp_1 (.A(A[1]), .B(B[1]), .A_B(comp_1_a_b), .A__B(comp_1_a__b));  // open: A_B_2
  comp comp_2 (.A(A[0]), .B(B[0]), .A_B(comp_2_a_b), .A__B(comp_2_a__b));  // open: A_B_2
  or or_1 (A___B, comp_1_a_b, and_1_out);
  and and_1 (and_1_out, comp_1_a__b, comp_2_a_b);
  and and_2 (A____B, comp_1_a__b, comp_2_a__b);
  nor nor_1 (A___B_2, A___B, A____B);
endmodule

module comp4 (
  input  [3:0] A,
  input  [3:0] B,
  output A___B,
  output A____B,
  output A___B_2
);

  wire and_1_out, comp2_1_a____b, comp2_1_a___b, comp2_2_a____b, comp2_2_a___b;

  comp2 comp2_1 (.A___B(comp2_1_a___b), .A____B(comp2_1_a____b), .A(A[3:2]), .B(B[3:2]));  // open: A___B_2
  comp2 comp2_2 (.A___B(comp2_2_a___b), .A____B(comp2_2_a____b), .A(A[1:0]), .B(B[1:0]));  // open: A___B_2
  or or_1 (A___B, comp2_1_a___b, and_1_out);
  and and_1 (and_1_out, comp2_1_a____b, comp2_2_a___b);
  and and_2 (A____B, comp2_1_a____b, comp2_2_a____b);
  nor nor_1 (A___B_2, A___B, A____B);
endmodule

module comp8 (
  input  [7:0] A,
  input  [7:0] B,
  output A___B,
  output A____B,
  output A___B_2
);

  wire and_1_out, comp4_1_a____b, comp4_1_a___b, comp4_2_a____b, comp4_2_a___b;

  comp4 comp4_1 (.A(A[7:4]), .B(B[7:4]), .A___B(comp4_1_a___b), .A____B(comp4_1_a____b));  // open: A___B_2
  comp4 comp4_2 (.A(A[3:0]), .B(B[3:0]), .A___B(comp4_2_a___b), .A____B(comp4_2_a____b));  // open: A___B_2
  or or_1 (A___B, comp4_1_a___b, and_1_out);
  and and_1 (and_1_out, comp4_1_a____b, comp4_2_a___b);
  and and_2 (A____B, comp4_1_a____b, comp4_2_a____b);
  nor nor_1 (A___B_2, A___B, A____B);
endmodule

module comp16 (
  input  [15:0] A,
  input  [15:0] B,
  output A___B,
  output A____B,
  output A___B_2
);

  wire and_1_out, comp8_1_a____b, comp8_1_a___b, comp8_2_a____b, comp8_2_a___b;

  comp8 comp8_1 (.A(A[15:8]), .B(B[15:8]), .A___B(comp8_1_a___b), .A____B(comp8_1_a____b));  // open: A___B_2
  comp8 comp8_2 (.A(A[7:0]), .B(B[7:0]), .A___B(comp8_2_a___b), .A____B(comp8_2_a____b));  // open: A___B_2
  and and_1 (and_1_out, comp8_1_a____b, comp8_2_a___b);
  or or_1 (A___B, comp8_1_a___b, and_1_out);
  and and_2 (A____B, comp8_1_a____b, comp8_2_a____b);
  nor nor_1 (A___B_2, A___B, A____B);
endmodule

module comp32 (
  input  [31:0] A,
  input  [31:0] B,
  output A___B,
  output A____B,
  output A___B_2
);

  wire and_1_out, comp16_1_a____b, comp16_1_a___b, comp16_2_a____b, comp16_2_a___b;

  comp16 comp16_1 (.A(A[31:16]), .B(B[31:16]), .A___B(comp16_1_a___b), .A____B(comp16_1_a____b));  // open: A___B_2
  comp16 comp16_2 (.A(A[15:0]), .B(B[15:0]), .A___B(comp16_2_a___b), .A____B(comp16_2_a____b));  // open: A___B_2
  and and_1 (and_1_out, comp16_1_a____b, comp16_2_a___b);
  or or_1 (A___B, comp16_1_a___b, and_1_out);
  and and_2 (A____B, comp16_1_a____b, comp16_2_a____b);
  nor nor_1 (A___B_2, A___B, A____B);
endmodule
