// Logisim project nasob.circ as structural Verilog: 4 circuits, main circuit main
module main (
  input  in_1,
  input  in_2,
  output out_3
);

  and and_1 (out_3, in_1, in_2);
endmodule

module nasob1 (
  input  in_1,
  input  in_2,
  output out_3
);

  and and_1 (out_3, in_1, in_2);
endmodule

module nasob2 (
  input  [1:0] in_1,
  input  [1:0] in_2,
  output [1:0] out_3,
  output [1:0] out_4
);

  wire adder_1_cout, and_1_out, and_2_out, and_3_out;

  and and_1 (and_1_out, in_1[1], in_2[0]);
  and and_2 (and_2_out, in_1[0], in_2[1]);
  and and_3 (and_3_out, in_2[1], in_1[1]);
  and and_4 (out_3[0], in_1[0], in_2[0]);
  Adder #(.width(1)) adder_1 (.a(and_1_out), .b(and_2_out), .out(out_3[1]), .cout(adder_1_cout));  // open: cin
  Adder #(.width(1)) adder_2 (.a(adder_1_cout), .b(and_3_out), .out(out_4[0]), .cout(out_4[1]));  // open: cin
endmodule

module nasob4 (
  input  [3:0] in_1,
  input  [3:0] in_2,
  output [3:0] out_3,
  output [3:0] out_4
);

  wire adder_1_cout, adder_2_cout, and_2_out, and_3_out, and_4_out, and_5_out;
  wire [1:0] nasob2_1_out_3, nasob2_1_out_4, nasob2_2_out_3, nasob2_2_out_4;

  nasob2 nasob2_1 (.in_1(in_1[1:0]), .in_2(in_2[1:0]), .out_3(nasob2_1_out_3), .out_4(nasob2_1_out_4));
  nasob2 nasob2_2 (.in_1(in_1[3:2]), .in_2(in_2[3:2]), .out_3(nasob2_2_out_3), .out_4(nasob2_2_out_4));
  and and_1 (out_3[0], in_1[0], in_2[0]);
  and and_2 (and_2_out, in_1[1], in_2[0]);
  and and_3 (and_3_out, in_1[0], in_2[2]);
  and and_4 (and_4_out, in_2[2], in_1[1]);
  and and_5 (and_5_out, in_2[0], in_1[2]);
  // AND_Gate and_6 is placed but not wired
  // AND_Gate and_7 is placed but not wired
  Adder #(.width(1)) adder_1 (.a(and_2_out), .b(and_3_out), .out(out_3[1]), .cout(adder_1_cout));  // open: cin
  Adder #(.width(1)) adder_2 (.a(adder_1_cout), .b(and_4_out), .out(out_3[2]), .cout(adder_2_cout));  // open: cin
  Adder #(.width(1)) adder_3 (.a(adder_2_cout), .b(and_5_out));  // open: out, cin, cout
endmodule
